// Logisim project ex4.circ as structural Verilog: 1 circuit, main circuit Split
module Split (
  input  [7:0] In1,
  output Out1,
  output [7:0] Out2
);

  wire [7:0] adder_1_out, not_1_out;

  assign not_1_out = ~In1;  // NOT_Gate not_1, 8 bits wide
  Adder adder_1 (.a(not_1_out), .b(8'h1), .out(adder_1_out));  // open: cin, cout
  and and_1 (Out1, In1[0], In1[7]);
  Multiplexer #(.enable("false"), .width(8)) multiplexer_1 (
    .in0({1'b1, In1[6:0]}), .in1(adder_1_out), .out(Out2), .sel(In1[7]));

  // Notes on the sheet:
  //   PUT CIRCUITRY HERE
endmodule
